# Fritzing sketch Termostato (saved by Fritzing 0.9.0b)
circuit board: 8.46667cm x 5.64444cm
breadboards: 1

parts:
  Componente1 = Arduino Uno (Rev3)
  LCD1 = LCD screen
  R2 = Trimmer Potentiometer [maximum_resistance=10kΩ package=THT]
  R3 = Temperature Sensor (Thermistor) [thermistor_type=NTC package=THT]
  R4 = Resistor [tolerance=±5% resistance=10k package=THT]
  RHT1 = Humidity and Temperature Sensor RHT03
  S1 = Momentary Switch [package=ksa_sealed_tac_switch]
  S2 = Momentary Switch [package=ksa_sealed_tac_switch]
  R5 = Resistor [tolerance=±5% resistance=10k package="1206 [SMD]"]
  R6 = Resistor [tolerance=±5% resistance=10k package="1206 [SMD]"]
  S3 = Momentary Switch [package=ksa_sealed_tac_switch]
  LED1 = smd LED [color="Blue (430nm)" package="0603 [SMD]"]
  R7 = Resistor [tolerance=±5% resistance=220 package="1206 [SMD]"]

nets:
  N1: Componente1.A0, R3.pin_1, R4.Pin_0
  N2: Componente1.D8, LCD1.E
  N3: Componente1.D9_PWM, LCD1.DB4
  N4: Componente1.D10_PWM/SS, LCD1.DB5
  N5: Componente1.D11_PWM/MOSI, LCD1.DB6
  N6: Componente1.D12/MISO, LCD1.DB7
  GND: Componente1.GND, LCD1.VSS, LCD1.R/W, LCD1.LED-, R2.leg1, R4.Pin_1, RHT1.GND, S1.3, S1.4, R5.Pin_1, R6.Pin_1
  N7: Componente1.D3_PWM, RHT1.Data-signal
  N8: Componente1.D4, R7.Pin_0
  N9: Componente1.D5_PWM, S2.1, R5.Pin_0
  N10: Componente1.D6_PWM, R6.Pin_0, S3.1
  N11: Componente1.D7, LCD1.RS
  N12: Componente1.RESET, S1.1, S1.2
  5V: Componente1.5V, LCD1.VDD, LCD1.LED+, R2.leg2, R3.pin_0, RHT1.Vcc, S2.3, S3.3, LED1.cathode
  N13: LCD1.V0, R2.wiper
  N14: LED1.anode, R7.Pin_1

notes:
  Sensore di umdità e temperatura: DHT11
  T+
  RESET
  T-

custom parts:
  Humidity and Temperature Sensor RHT03: Digital relative humidity & temperature sensor RHT03
